# Fritzing sketch AR17_4led (saved by Fritzing 0.9.3b)
breadboards: 1

parts:
  부품1 = Arduino Uno (Rev3)
  R1 = Resistor [tolerance=±5% resistance=330 package=THT]  # not connected
  LED1 = LED - 5mm [color="Red (633nm)" package="5 mm [THT]"]
  LED2 = LED - 5mm [color="Green (570nm)" package="5 mm [THT]"]
  R3 = Resistor [tolerance=±5% resistance=330 package=THT]  # not connected
  LED3 = LED - 5mm [color="Yellow (595nm)" package="5 mm [THT]"]
  LED4 = LED - 5mm [color="Blue (430nm)" package="5 mm [THT]"]
  R4 = Resistor [tolerance=±5% resistance=330 package=THT]
  R5 = Resistor [tolerance=±5% resistance=330 package=THT]

nets:
  N1: 부품1.D9_PWM, LED3.anode
  N2: 부품1.D3_PWM, LED2.anode
  N3: 부품1.D5_PWM, LED1.anode
  N4: 부품1.D6_PWM, LED4.anode
  N5: 부품1.GND, R4.Pin_1, R5.Pin_1
  N6: LED3.cathode, R4.Pin_0
  N7: LED4.cathode, R5.Pin_0
